// Logisim project ALU.circ as structural Verilog: 7 circuits, main circuit ALU
module ALU (
  input  [31:0] A,
  input  [31:0] B,
  input  [3:0] OP,
  output [31:0] Y,
  output EQ,
  output LT,
  output LTU
);

  wire and_1_out, and_2_out, not_1_out, or_1_out;
  wire [0:0] multiplexer_2_out;
  wire [31:0] addsub_1_y, and_3_out, multiplexer_1_out, or_2_out, shift_1_y, xor_1_out;

  and and_1 (and_1_out, OP[0], ~OP[1], ~OP[2]);  // AND_Gate
  or or_1 (or_1_out, and_1_out, OP[3]);
  and and_2 (and_2_out, OP[1], OP[0]);
  not not_1 (not_1_out, OP[1]);
  AddSub addsub_1 (.Cin(or_1_out), .A(A), .B(B), .Y(addsub_1_y), .EQ(EQ), .LT(LT), .LTU(LTU));  // open: Cout, V
  assign and_3_out = A & B;  // AND_Gate and_3, 32 bits wide
  assign or_2_out = A | B;  // OR_Gate or_2, 32 bits wide
  assign xor_1_out = A ^ B;  // XOR_Gate xor_1, 32 bits wide
  Shift shift_1 (.arith(and_2_out), .left(not_1_out), .s(B[4:0]), .X(A), .Y(shift_1_y));
  Multiplexer #(.select(3), .width(32)) multiplexer_1 (
    .in0(addsub_1_y), .in1(addsub_1_y), .in2(and_3_out), .in3(or_2_out), .in4(xor_1_out), .in5(shift_1_y),
    .in6(shift_1_y), .in7(shift_1_y), .out(multiplexer_1_out), .sel(OP[2:0]));
  Multiplexer multiplexer_2 (.in0(LT), .in1(LTU), .out(multiplexer_2_out[0]), .sel(OP[0]));
  Multiplexer #(.width(32)) multiplexer_3 (
    .in0(multiplexer_1_out), .in1({{31{1'b0}}, multiplexer_2_out[0]}), .out(Y), .sel(OP[3]));
endmodule

module Shift (
  input  [31:0] X,
  input  arith,
  input  left,
  input  [4:0] s,
  output [31:0] Y
);

  wire [15:0] multiplexer_5_out;
  wire [31:0] multiplexer_1_out, multiplexer_2_out, multiplexer_3_out, multiplexer_4_out,
       multiplexer_5_out_2, multiplexer_6_out, reverse32_1_xout, reverse32_2_xout;

  Reverse32 reverse32_1 (.Xin(X), .Xout(reverse32_1_xout));
  and and_1 (multiplexer_5_out_2[31], X[31], arith, ~left);  // AND_Gate
  Multiplexer #(.width(32)) multiplexer_1 (.in0(X), .in1(reverse32_1_xout), .out(multiplexer_1_out), .sel(left));
  Multiplexer #(.width(32)) multiplexer_2 (
    .in0(multiplexer_1_out), .in1({multiplexer_5_out_2[31], multiplexer_1_out[31:1]}),
    .out(multiplexer_2_out), .sel(s[0]));
  Multiplexer #(.width(32)) multiplexer_3 (
    .in0(multiplexer_2_out), .in1({{2{multiplexer_5_out_2[31]}}, multiplexer_2_out[31:2]}),
    .out(multiplexer_3_out), .sel(s[1]));
  Multiplexer #(.width(32)) multiplexer_4 (
    .in0(multiplexer_3_out), .in1({{4{multiplexer_5_out_2[31]}}, multiplexer_3_out[31:4]}),
    .out(multiplexer_4_out), .sel(s[2]));
  Multiplexer #(.width(32)) multiplexer_5 (
    .in0(multiplexer_4_out), .in1({{8{multiplexer_5_out_2[31]}}, multiplexer_4_out[31:8]}),
    .out({multiplexer_5_out_2[15:0], multiplexer_5_out}), .sel(s[3]));
  Multiplexer #(.width(32)) multiplexer_6 (
    .in0({multiplexer_5_out_2[15:0], multiplexer_5_out}),
    .in1({{16{multiplexer_5_out_2[31]}}, multiplexer_5_out_2[15:0]}), .out(multiplexer_6_out), .sel(s[4]));
  Reverse32 reverse32_2 (.Xin(multiplexer_6_out), .Xout(reverse32_2_xout));
  Multiplexer #(.width(32)) multiplexer_7 (.in0(multiplexer_6_out), .in1(reverse32_2_xout), .out(Y), .sel(left));
endmodule

module Reverse32 (
  input  [31:0] Xin,
  output [31:0] Xout
);


  assign Xout = {Xin[0], Xin[1], Xin[2], Xin[3], Xin[4], Xin[5], Xin[6], Xin[7], Xin[8], Xin[9], Xin[10], Xin[11], Xin[12], Xin[13], Xin[14], Xin[15], Xin[16], Xin[17], Xin[18], Xin[19], Xin[20], Xin[21], Xin[22], Xin[23], Xin[24], Xin[25], Xin[26], Xin[27], Xin[28], Xin[29], Xin[30], Xin[31]};
endmodule

module AddSub (
  input  [31:0] A,
  input  [31:0] B,
  input  Cin,
  output [31:0] Y,
  output Cout,
  output V,
  output EQ,
  output LT,
  output LTU
);

  wire [31:0] twoscomp_1_bout;

  TwosComp twoscomp_1 (.Bin(B), .Cin(Cin), .Bout(twoscomp_1_bout));
  Add32 add32_1 (.Cin(Cin), .A(A), .B(twoscomp_1_bout), .Y(Y), .Cout(Cout), .V(V), .EQ(EQ), .LT(LT), .LTU(LTU));
endmodule

module TwosComp (
  input  [31:0] Bin,
  input  Cin,
  output [31:0] Bout
);

  xor xor_1 (Bout[0], Bin[0], Cin);
  xor xor_2 (Bout[1], Bin[1], Cin);
  xor xor_3 (Bout[2], Bin[2], Cin);
  xor xor_4 (Bout[3], Bin[3], Cin);
  xor xor_5 (Bout[4], Bin[4], Cin);
  xor xor_6 (Bout[5], Bin[5], Cin);
  xor xor_7 (Bout[6], Bin[6], Cin);
  xor xor_8 (Bout[7], Bin[7], Cin);
  xor xor_9 (Bout[8], Bin[8], Cin);
  xor xor_10 (Bout[9], Bin[9], Cin);
  xor xor_11 (Bout[10], Bin[10], Cin);
  xor xor_12 (Bout[11], Bin[11], Cin);
  xor xor_13 (Bout[12], Bin[12], Cin);
  xor xor_14 (Bout[13], Bin[13], Cin);
  xor xor_15 (Bout[14], Bin[14], Cin);
  xor xor_16 (Bout[15], Bin[15], Cin);
  xor xor_17 (Bout[16], Bin[16], Cin);
  xor xor_18 (Bout[17], Bin[17], Cin);
  xor xor_19 (Bout[18], Bin[18], Cin);
  xor xor_20 (Bout[19], Bin[19], Cin);
  xor xor_21 (Bout[20], Bin[20], Cin);
  xor xor_22 (Bout[21], Bin[21], Cin);
  xor xor_23 (Bout[22], Bin[22], Cin);
  xor xor_24 (Bout[23], Bin[23], Cin);
  xor xor_25 (Bout[24], Bin[24], Cin);
  xor xor_26 (Bout[25], Bin[25], Cin);
  xor xor_27 (Bout[26], Bin[26], Cin);
  xor xor_28 (Bout[27], Bin[27], Cin);
  xor xor_29 (Bout[28], Bin[28], Cin);
  xor xor_30 (Bout[29], Bin[29], Cin);
  xor xor_31 (Bout[30], Bin[30], Cin);
  xor xor_32 (Bout[31], Bin[31], Cin);
endmodule

module Add32 (
  input  [31:0] A,
  input  [31:0] B,
  input  Cin,
  output [31:0] Y,
  output Cout,
  output V,
  output EQ,
  output LT,
  output LTU
);

  wire fulladder_1_cout, fulladder_2_cout, fulladder_3_cout, fulladder_4_cout, fulladder_5_cout,
       fulladder_6_cout, fulladder_7_cout, fulladder_8_cout, fulladder_9_cout, fulladder_10_cout,
       fulladder_11_cout, fulladder_12_cout, fulladder_13_cout, fulladder_14_cout, fulladder_15_cout,
       fulladder_16_cout, fulladder_17_cout, fulladder_18_cout, fulladder_19_cout, fulladder_20_cout,
       fulladder_21_cout, fulladder_22_cout, fulladder_23_cout, fulladder_24_cout, fulladder_25_cout,
       fulladder_26_cout, fulladder_27_cout, fulladder_28_cout, fulladder_29_cout, fulladder_30_cout,
       fulladder_31_cout;

  FullAdder fulladder_1 (.A(A[0]), .B(B[0]), .Cin(Cin), .Y(Y[0]), .Cout(fulladder_1_cout));
  FullAdder fulladder_2 (.A(A[1]), .B(B[1]), .Cin(fulladder_1_cout), .Y(Y[1]), .Cout(fulladder_2_cout));
  FullAdder fulladder_3 (.A(A[2]), .B(B[2]), .Cin(fulladder_2_cout), .Y(Y[2]), .Cout(fulladder_3_cout));
  FullAdder fulladder_4 (.A(A[3]), .B(B[3]), .Cin(fulladder_3_cout), .Y(Y[3]), .Cout(fulladder_4_cout));
  FullAdder fulladder_5 (.A(A[4]), .B(B[4]), .Cin(fulladder_4_cout), .Y(Y[4]), .Cout(fulladder_5_cout));
  FullAdder fulladder_6 (.A(A[5]), .B(B[5]), .Cin(fulladder_5_cout), .Y(Y[5]), .Cout(fulladder_6_cout));
  FullAdder fulladder_7 (.A(A[6]), .B(B[6]), .Cin(fulladder_6_cout), .Y(Y[6]), .Cout(fulladder_7_cout));
  FullAdder fulladder_8 (.A(A[7]), .B(B[7]), .Cin(fulladder_7_cout), .Y(Y[7]), .Cout(fulladder_8_cout));
  FullAdder fulladder_9 (.A(A[8]), .B(B[8]), .Cin(fulladder_8_cout), .Y(Y[8]), .Cout(fulladder_9_cout));
  FullAdder fulladder_10 (.A(A[9]), .B(B[9]), .Cin(fulladder_9_cout), .Y(Y[9]), .Cout(fulladder_10_cout));
  FullAdder fulladder_11 (.A(A[10]), .B(B[10]), .Cin(fulladder_10_cout), .Y(Y[10]), .Cout(fulladder_11_cout));
  FullAdder fulladder_12 (.A(A[11]), .B(B[11]), .Cin(fulladder_11_cout), .Y(Y[11]), .Cout(fulladder_12_cout));
  FullAdder fulladder_13 (.A(A[12]), .B(B[12]), .Cin(fulladder_12_cout), .Y(Y[12]), .Cout(fulladder_13_cout));
  FullAdder fulladder_14 (.A(A[13]), .B(B[13]), .Cin(fulladder_13_cout), .Y(Y[13]), .Cout(fulladder_14_cout));
  FullAdder fulladder_15 (.A(A[14]), .B(B[14]), .Cin(fulladder_14_cout), .Y(Y[14]), .Cout(fulladder_15_cout));
  FullAdder fulladder_16 (.A(A[15]), .B(B[15]), .Cin(fulladder_15_cout), .Y(Y[15]), .Cout(fulladder_16_cout));
  FullAdder fulladder_17 (.A(A[16]), .B(B[16]), .Cin(fulladder_16_cout), .Y(Y[16]), .Cout(fulladder_17_cout));
  FullAdder fulladder_18 (.A(A[17]), .B(B[17]), .Cin(fulladder_17_cout), .Y(Y[17]), .Cout(fulladder_18_cout));
  FullAdder fulladder_19 (.A(A[18]), .B(B[18]), .Cin(fulladder_18_cout), .Y(Y[18]), .Cout(fulladder_19_cout));
  FullAdder fulladder_20 (.A(A[19]), .B(B[19]), .Cin(fulladder_19_cout), .Y(Y[19]), .Cout(fulladder_20_cout));
  FullAdder fulladder_21 (.A(A[20]), .B(B[20]), .Cin(fulladder_20_cout), .Y(Y[20]), .Cout(fulladder_21_cout));
  FullAdder fulladder_22 (.A(A[21]), .B(B[21]), .Cin(fulladder_21_cout), .Y(Y[21]), .Cout(fulladder_22_cout));
  FullAdder fulladder_23 (.A(A[22]), .B(B[22]), .Cin(fulladder_22_cout), .Y(Y[22]), .Cout(fulladder_23_cout));
  FullAdder fulladder_24 (.A(A[23]), .B(B[23]), .Cin(fulladder_23_cout), .Y(Y[23]), .Cout(fulladder_24_cout));
  FullAdder fulladder_25 (.A(A[24]), .B(B[24]), .Cin(fulladder_24_cout), .Y(Y[24]), .Cout(fulladder_25_cout));
  FullAdder fulladder_26 (.A(A[25]), .B(B[25]), .Cin(fulladder_25_cout), .Y(Y[25]), .Cout(fulladder_26_cout));
  FullAdder fulladder_27 (.A(A[26]), .B(B[26]), .Cin(fulladder_26_cout), .Y(Y[26]), .Cout(fulladder_27_cout));
  FullAdder fulladder_28 (.A(A[27]), .B(B[27]), .Cin(fulladder_27_cout), .Y(Y[27]), .Cout(fulladder_28_cout));
  FullAdder fulladder_29 (.A(A[28]), .B(B[28]), .Cin(fulladder_28_cout), .Y(Y[28]), .Cout(fulladder_29_cout));
  FullAdder fulladder_30 (.A(A[29]), .B(B[29]), .Cin(fulladder_29_cout), .Y(Y[29]), .Cout(fulladder_30_cout));
  FullAdder fulladder_31 (.A(A[30]), .B(B[30]), .Cin(fulladder_30_cout), .Y(Y[30]), .Cout(fulladder_31_cout));
  FullAdder fulladder_32 (.A(A[31]), .B(B[31]), .Cin(fulladder_31_cout), .Y(Y[31]), .Cout(Cout));
  xor xor_1 (V, Cout, fulladder_31_cout);
  not not_1 (LTU, Cout);
  nor nor_1 (EQ, Y[0], Y[1], Y[2], Y[3], Y[4], Y[5], Y[6], Y[7], Y[8], Y[9], Y[10], Y[11], Y[12], Y[13], Y[14], Y[15], Y[16], Y[17], Y[18], Y[19], Y[20], Y[21], Y[22], Y[23], Y[24], Y[25], Y[26], Y[27], Y[28], Y[29], Y[30], Y[31]);
  xor xor_2 (LT, V, Y[31]);
endmodule

module FullAdder (
  input  A,
  input  B,
  input  Cin,
  output Y,
  output Cout
);

  wire and_1_out, and_2_out, xor_1_out;

  xor xor_1 (xor_1_out, A, B);
  xor xor_2 (Y, xor_1_out, Cin);
  and and_1 (and_1_out, A, B);
  and and_2 (and_2_out, Cin, xor_1_out);
  or or_1 (Cout, and_1_out, and_2_out);
endmodule
