// Logisim project CPU.circ as structural Verilog: 3 circuits, main circuit CPU
module CPU (
  input  rst,
  input  [4:0] dbg,
  output [31:0] dbg_val
);

  wire and_1_out, clock_1_out, cu_1_alur, cu_1_ir_we, cu_1_pc_we, cu_1_rf_we, cu_1_v, d_ff_1_q, d_ff_1_qn,
       d_ff_2_q, or_1_out;
  wire [1:0] cu_1_a_sel, cu_1_b_sel, cu_1_imm_sel;
  wire [3:0] cu_1_op, multiplexer_4_out;
  wire [4:0] multiplexer_1_out;
  wire [31:0] alu_1_y, immgen_1_imm, multiplexer_2_out, multiplexer_3_out, regfile_1_o2, register32_1_o,
       register32_2_o, rom_1_data;

  ROM #(.addrWidth(10), .dataWidth(32)) rom_1 (.addr(register32_2_o[11:2]), .data(rom_1_data));
  Clock clock_1 (.out(clock_1_out));
  Multiplexer #(.width(5)) multiplexer_1 (
    .in0(register32_1_o[20:16]), .in1(dbg), .out(multiplexer_1_out), .sel(d_ff_2_q));
  Register32 register32_1 (.d(rom_1_data), .en(cu_1_ir_we), .clk(clock_1_out), .o(register32_1_o));
  D_Flip_Flop d_ff_1 (.D(d_ff_1_qn), .clk(clock_1_out), .Q(d_ff_1_q), .Qn(d_ff_1_qn), .reset(rst));  // open: preset
  Register32 register32_2 (.d(alu_1_y), .en(cu_1_pc_we), .clk(clock_1_out), .o(register32_2_o));
  ImmGen immgen_1 (.sel(cu_1_imm_sel), .ir(register32_1_o), .imm(immgen_1_imm));
  RegFile regfile_1 (
    .r1(multiplexer_1_out), .data(alu_1_y), .we(cu_1_rf_we), .w(register32_1_o[25:21]), .clk(clock_1_out),
    .r2(register32_1_o[15:11]), .o2(regfile_1_o2), .o1(dbg_val));
  CU cu_1 (
    .opcode(register32_1_o[31:26]), .ex(d_ff_1_q), .hlt(d_ff_2_q), .a_sel(cu_1_a_sel), .b_sel(cu_1_b_sel),
    .imm_sel(cu_1_imm_sel), .op(cu_1_op), .v(cu_1_v), .alur(cu_1_alur), .ir_we(cu_1_ir_we),
    .pc_we(cu_1_pc_we), .rf_we(cu_1_rf_we));
  Multiplexer #(.select(2), .width(32)) multiplexer_2 (
    .in0(dbg_val), .in1(register32_2_o), .in2({32{1'b0}}), .out(multiplexer_2_out), .sel(cu_1_a_sel));  // open: in3
  Multiplexer #(.select(2), .width(32)) multiplexer_3 (
    .in0(regfile_1_o2), .in1(32'h4), .in2(immgen_1_imm), .out(multiplexer_3_out), .sel(cu_1_b_sel));  // open: in3
  Multiplexer #(.width(4)) multiplexer_4 (
    .in0(cu_1_op), .in1(register32_1_o[3:0]), .out(multiplexer_4_out), .sel(cu_1_alur));
  and and_1 (and_1_out, d_ff_1_q, ~cu_1_v);  // AND_Gate
  D_Flip_Flop d_ff_2 (.D(or_1_out), .clk(clock_1_out), .Q(d_ff_2_q), .reset(rst));  // open: Qn, preset
  or or_1 (or_1_out, d_ff_2_q, and_1_out);
  ALU alu_1 (.OP(multiplexer_4_out), .A(multiplexer_2_out), .B(multiplexer_3_out), .Y(alu_1_y));  // open: EQ, LT, LTU

  // Notes on the sheet:
  //   contents of rom_1 (hex, n*v repeats v):
  //   2822468a 4210678 440ffff 611002 811004 1ca10004 24c40008 20e40008 1020808 1220809 1411001 1611004
  //   16b1804 16b2004 16b2804 16b3004 16b3804 16b4004 16b4804 16b5004 cc000000
endmodule

module CU (
  input  hlt,
  input  ex,
  input  [5:0] opcode,
  output ir_we,
  output pc_we,
  output rf_we,
  output [1:0] a_sel,
  output [1:0] b_sel,
  output [1:0] imm_sel,
  output [3:0] op,
  output v,
  output alur
);

  wire [2:0] multiplexer_2_out;
  wire [14:0] multiplexer_1_out;

  Multiplexer #(.select(6), .width(15)) multiplexer_1 (
    .in0(15'h6004), .in1(15'h2044), .in2(15'h2444), .in3(15'h2644), .in4(15'h2844), .in5(15'h3044),
    .in6(15'h3244), .in7(15'h2a44), .in8(15'h2c44), .in9(15'h2e44), .in10(15'h2154), .in11({15{1'b0}}),
    .in12({15{1'b0}}), .in13({15{1'b0}}), .in14({15{1'b0}}), .in15({15{1'b0}}), .in16({15{1'b0}}),
    .in17({15{1'b0}}), .in18({15{1'b0}}), .in19({15{1'b0}}), .in20({15{1'b0}}), .in21({15{1'b0}}),
    .in22({15{1'b0}}), .in23({15{1'b0}}), .in24({15{1'b0}}), .in25({15{1'b0}}), .in26({15{1'b0}}),
    .in27({15{1'b0}}), .in28({15{1'b0}}), .in29({15{1'b0}}), .in30({15{1'b0}}), .in31({15{1'b0}}),
    .in32({15{1'b0}}), .in33({15{1'b0}}), .in34({15{1'b0}}), .in35({15{1'b0}}), .in36({15{1'b0}}),
    .in37({15{1'b0}}), .in38({15{1'b0}}), .in39({15{1'b0}}), .in40({15{1'b0}}), .in41({15{1'b0}}),
    .in42({15{1'b0}}), .in43({15{1'b0}}), .in44({15{1'b0}}), .in45({15{1'b0}}), .in46({15{1'b0}}),
    .in47({15{1'b0}}), .in48({15{1'b0}}), .in49({15{1'b0}}), .in50({15{1'b0}}), .in51({15{1'b0}}),
    .in52({15{1'b0}}), .in53({15{1'b0}}), .in54({15{1'b0}}), .in55({15{1'b0}}), .in56({15{1'b0}}),
    .in57({15{1'b0}}), .in58({15{1'b0}}), .in59({15{1'b0}}), .in60({15{1'b0}}), .in61({15{1'b0}}),
    .in62({15{1'b0}}), .in63({15{1'b0}}), .out(multiplexer_1_out), .sel(opcode));
  Multiplexer #(.width(15)) multiplexer_2 (
    .in0(15'h202b), .in1(multiplexer_1_out), .out({alur, v, op, imm_sel, b_sel, a_sel, multiplexer_2_out}),
    .sel(ex));
  and and_1 (ir_we, ~hlt, multiplexer_2_out[0]);  // AND_Gate
  and and_2 (pc_we, ~hlt, multiplexer_2_out[1]);  // AND_Gate
  and and_3 (rf_we, ~hlt, multiplexer_2_out[2]);  // AND_Gate
endmodule

module ImmGen (
  input  [1:0] sel,
  input  [31:0] ir,
  output [31:0] imm
);

  wire [31:0] bit_extender_1_out, bit_extender_2_out;

  assign bit_extender_1_out = {{16{ir[15]}}, ir[15:0]};  // Bit_Extender bit_extender_1
  assign bit_extender_2_out = {{11{ir[20]}}, ir[20:0]};  // Bit_Extender bit_extender_2
  Multiplexer #(.select(2), .width(32)) multiplexer_1 (
    .in0(bit_extender_1_out), .in1({bit_extender_1_out[29:0], 2'b00}), .in2({ir[20:0], {11{1'b0}}}),
    .in3({bit_extender_2_out[29:0], 2'b00}), .out(imm), .sel(sel));
endmodule
