// Logisim project RegFile.circ as structural Verilog: 3 circuits, main circuit RegFile
module RegFile (
  input  [4:0] r1,
  input  [31:0] data,
  input  we,
  input  [4:0] w,
  input  clk,
  input  [4:0] r2,
  output [31:0] o1,
  output [31:0] o2
);

  wire demultiplexer_1_out0, demultiplexer_1_out1, demultiplexer_1_out2, demultiplexer_1_out3,
       demultiplexer_1_out4, demultiplexer_1_out5, demultiplexer_1_out6, demultiplexer_1_out7,
       demultiplexer_1_out8, demultiplexer_1_out9, demultiplexer_1_out10, demultiplexer_1_out11,
       demultiplexer_1_out12, demultiplexer_1_out13, demultiplexer_1_out14, demultiplexer_1_out15,
       demultiplexer_1_out16, demultiplexer_1_out17, demultiplexer_1_out18, demultiplexer_1_out19,
       demultiplexer_1_out20, demultiplexer_1_out21, demultiplexer_1_out22, demultiplexer_1_out23,
       demultiplexer_1_out24, demultiplexer_1_out25, demultiplexer_1_out26, demultiplexer_1_out27,
       demultiplexer_1_out28, demultiplexer_1_out29, demultiplexer_1_out30, demultiplexer_1_out31;
  wire [31:0] register32_1_o, register32_2_o, register32_3_o, register32_4_o, register32_5_o, register32_6_o,
       register32_7_o, register32_8_o, register32_9_o, register32_10_o, register32_11_o, register32_12_o,
       register32_13_o, register32_14_o, register32_15_o, register32_16_o, register32_17_o, register32_18_o,
       register32_19_o, register32_20_o, register32_21_o, register32_22_o, register32_23_o, register32_24_o,
       register32_25_o, register32_26_o, register32_27_o, register32_28_o, register32_29_o, register32_30_o,
       register32_31_o;

  Demultiplexer #(.select(5)) demultiplexer_1 (
    .out0(demultiplexer_1_out0), .out1(demultiplexer_1_out1), .out2(demultiplexer_1_out2),
    .out3(demultiplexer_1_out3), .out4(demultiplexer_1_out4), .out5(demultiplexer_1_out5),
    .out6(demultiplexer_1_out6), .out7(demultiplexer_1_out7), .out8(demultiplexer_1_out8),
    .out9(demultiplexer_1_out9), .out10(demultiplexer_1_out10), .out11(demultiplexer_1_out11),
    .out12(demultiplexer_1_out12), .out13(demultiplexer_1_out13), .out14(demultiplexer_1_out14),
    .out15(demultiplexer_1_out15), .out16(demultiplexer_1_out16), .out17(demultiplexer_1_out17),
    .out18(demultiplexer_1_out18), .out19(demultiplexer_1_out19), .out20(demultiplexer_1_out20),
    .out21(demultiplexer_1_out21), .out22(demultiplexer_1_out22), .out23(demultiplexer_1_out23),
    .out24(demultiplexer_1_out24), .out25(demultiplexer_1_out25), .out26(demultiplexer_1_out26),
    .out27(demultiplexer_1_out27), .out28(demultiplexer_1_out28), .out29(demultiplexer_1_out29),
    .out30(demultiplexer_1_out30), .out31(demultiplexer_1_out31), .in(we), .sel(w));
  Register32 register32_1 (.d(data), .en(demultiplexer_1_out1), .clk(clk), .o(register32_1_o));
  Register32 register32_2 (.d(data), .en(demultiplexer_1_out2), .clk(clk), .o(register32_2_o));
  Register32 register32_3 (.d(data), .en(demultiplexer_1_out3), .clk(clk), .o(register32_3_o));
  Register32 register32_4 (.d(data), .en(demultiplexer_1_out4), .clk(clk), .o(register32_4_o));
  Register32 register32_5 (.d(data), .en(demultiplexer_1_out5), .clk(clk), .o(register32_5_o));
  Register32 register32_6 (.d(data), .en(demultiplexer_1_out6), .clk(clk), .o(register32_6_o));
  Register32 register32_7 (.d(data), .en(demultiplexer_1_out7), .clk(clk), .o(register32_7_o));
  Register32 register32_8 (.d(data), .en(demultiplexer_1_out8), .clk(clk), .o(register32_8_o));
  Register32 register32_9 (.d(data), .en(demultiplexer_1_out9), .clk(clk), .o(register32_9_o));
  Register32 register32_10 (.d(data), .en(demultiplexer_1_out10), .clk(clk), .o(register32_10_o));
  Register32 register32_11 (.d(data), .en(demultiplexer_1_out11), .clk(clk), .o(register32_11_o));
  Register32 register32_12 (.d(data), .en(demultiplexer_1_out12), .clk(clk), .o(register32_12_o));
  Register32 register32_13 (.d(data), .en(demultiplexer_1_out13), .clk(clk), .o(register32_13_o));
  Register32 register32_14 (.d(data), .en(demultiplexer_1_out14), .clk(clk), .o(register32_14_o));
  Register32 register32_15 (.d(data), .en(demultiplexer_1_out15), .clk(clk), .o(register32_15_o));
  Register32 register32_16 (.d(data), .en(demultiplexer_1_out16), .clk(clk), .o(register32_16_o));
  Register32 register32_17 (.d(data), .en(demultiplexer_1_out17), .clk(clk), .o(register32_17_o));
  Register32 register32_18 (.d(data), .en(demultiplexer_1_out18), .clk(clk), .o(register32_18_o));
  Register32 register32_19 (.d(data), .en(demultiplexer_1_out19), .clk(clk), .o(register32_19_o));
  Register32 register32_20 (.d(data), .en(demultiplexer_1_out20), .clk(clk), .o(register32_20_o));
  Register32 register32_21 (.d(data), .en(demultiplexer_1_out21), .clk(clk), .o(register32_21_o));
  Register32 register32_22 (.d(data), .en(demultiplexer_1_out22), .clk(clk), .o(register32_22_o));
  Register32 register32_23 (.d(data), .en(demultiplexer_1_out23), .clk(clk), .o(register32_23_o));
  Register32 register32_24 (.d(data), .en(demultiplexer_1_out24), .clk(clk), .o(register32_24_o));
  Register32 register32_25 (.d(data), .en(demultiplexer_1_out25), .clk(clk), .o(register32_25_o));
  Register32 register32_26 (.d(data), .en(demultiplexer_1_out26), .clk(clk), .o(register32_26_o));
  Register32 register32_27 (.d(data), .en(demultiplexer_1_out27), .clk(clk), .o(register32_27_o));
  Register32 register32_28 (.d(data), .en(demultiplexer_1_out28), .clk(clk), .o(register32_28_o));
  Register32 register32_29 (.d(data), .en(demultiplexer_1_out29), .clk(clk), .o(register32_29_o));
  Register32 register32_30 (.d(data), .en(demultiplexer_1_out30), .clk(clk), .o(register32_30_o));
  Register32 register32_31 (.d(data), .en(demultiplexer_1_out31), .clk(clk), .o(register32_31_o));
  Multiplexer #(.select(5), .width(32)) multiplexer_1 (
    .in0({32{1'b0}}), .in1(register32_1_o), .in2(register32_2_o), .in3(register32_3_o), .in4(register32_4_o),
    .in5(register32_5_o), .in6(register32_6_o), .in7(register32_7_o), .in8(register32_8_o),
    .in9(register32_9_o), .in10(register32_10_o), .in11(register32_11_o), .in12(register32_12_o),
    .in13(register32_13_o), .in14(register32_14_o), .in15(register32_15_o), .in16(register32_16_o),
    .in17(register32_17_o), .in18(register32_18_o), .in19(register32_19_o), .in20(register32_20_o),
    .in21(register32_21_o), .in22(register32_22_o), .in23(register32_23_o), .in24(register32_24_o),
    .in25(register32_25_o), .in26(register32_26_o), .in27(register32_27_o), .in28(register32_28_o),
    .in29(register32_29_o), .in30(register32_30_o), .in31(register32_31_o), .out(o1), .sel(r1));
  Multiplexer #(.select(5), .width(32)) multiplexer_2 (
    .in0({32{1'b0}}), .in1(register32_1_o), .in2(register32_2_o), .in3(register32_3_o), .in4(register32_4_o),
    .in5(register32_5_o), .in6(register32_6_o), .in7(register32_7_o), .in8(register32_8_o),
    .in9(register32_9_o), .in10(register32_10_o), .in11(register32_11_o), .in12(register32_12_o),
    .in13(register32_13_o), .in14(register32_14_o), .in15(register32_15_o), .in16(register32_16_o),
    .in17(register32_17_o), .in18(register32_18_o), .in19(register32_19_o), .in20(register32_20_o),
    .in21(register32_21_o), .in22(register32_22_o), .in23(register32_23_o), .in24(register32_24_o),
    .in25(register32_25_o), .in26(register32_26_o), .in27(register32_27_o), .in28(register32_28_o),
    .in29(register32_29_o), .in30(register32_30_o), .in31(register32_31_o), .out(o2), .sel(r2));
endmodule

module Register32 (
  input  [31:0] d,
  input  en,
  input  clk,
  output [31:0] o
);

  Byte byte_1 (.D(d[7:0]), .En(en), .Clk(clk), .O(o[7:0]));
  Byte byte_2 (.D(d[15:8]), .Clk(clk), .O(o[15:8]));  // open: En
  Byte byte_3 (.D(d[23:16]), .En(en), .Clk(clk), .O(o[23:16]));
  Byte byte_4 (.D(d[31:24]), .En(en), .Clk(clk), .O(o[31:24]));
endmodule

module Byte (
  input  En,
  input  Clk,
  input  [7:0] D,
  output [7:0] O
);

  wire multiplexer_1_out, multiplexer_2_out, multiplexer_3_out, multiplexer_4_out, multiplexer_5_out,
       multiplexer_6_out, multiplexer_7_out, multiplexer_8_out;

  D_Flip_Flop d_ff_1 (.D(multiplexer_1_out), .clk(Clk), .Q(O[0]));  // open: Qn, preset, reset
  Multiplexer multiplexer_1 (.in0(O[0]), .in1(D[0]), .out(multiplexer_1_out), .sel(En));
  D_Flip_Flop d_ff_2 (.D(multiplexer_2_out), .clk(Clk), .Q(O[1]));  // open: Qn, preset, reset
  Multiplexer multiplexer_2 (.in0(O[1]), .in1(D[1]), .out(multiplexer_2_out), .sel(En));
  Multiplexer multiplexer_3 (.in0(O[2]), .in1(D[2]), .out(multiplexer_3_out), .sel(En));
  D_Flip_Flop d_ff_3 (.D(multiplexer_3_out), .clk(Clk), .Q(O[2]));  // open: Qn, preset, reset
  D_Flip_Flop d_ff_4 (.D(multiplexer_4_out), .clk(Clk), .Q(O[3]));  // open: Qn, preset, reset
  Multiplexer multiplexer_4 (.in0(O[3]), .in1(D[3]), .out(multiplexer_4_out), .sel(En));
  D_Flip_Flop d_ff_5 (.D(multiplexer_5_out), .clk(Clk), .Q(O[4]));  // open: Qn, preset, reset
  Multiplexer multiplexer_5 (.in0(O[4]), .in1(D[4]), .out(multiplexer_5_out), .sel(En));
  D_Flip_Flop d_ff_6 (.D(multiplexer_6_out), .clk(Clk), .Q(O[5]));  // open: Qn, preset, reset
  Multiplexer multiplexer_6 (.in0(O[5]), .in1(D[5]), .out(multiplexer_6_out), .sel(En));
  D_Flip_Flop d_ff_7 (.D(multiplexer_7_out), .clk(Clk), .Q(O[6]));  // open: Qn, preset, reset
  Multiplexer multiplexer_7 (.in0(O[6]), .in1(D[6]), .out(multiplexer_7_out), .sel(En));
  D_Flip_Flop d_ff_8 (.D(multiplexer_8_out), .clk(Clk), .Q(O[7]));  // open: Qn, preset, reset
  Multiplexer multiplexer_8 (.in0(O[7]), .in1(D[7]), .out(multiplexer_8_out), .sel(En));
endmodule
